# Fritzing sketch exosuit_Lbw37qnw1X (saved by Fritzing 0.9.3b)

parts:
  Part1 = Arduino Uno (Rev3)
  Part2 = Bluetooth HC-05 Macho
  U1 = 4-Channel 5v Relay Shield [package=relay-4ch5v10a]
  M1 = Stepper Motor - Bipolar
  M2 = Stepper Motor - Bipolar

nets:
  N1: Part1.D0/RX, Part2.TXD
  N2: Part1.D1/TX, Part2.RXD
  5V: Part1.5V, Part2.VCC
  GND: Part1.GND, Part2.GND
  N3: U1.K1-In, M1.A
  N4: U1.K1-On, M2.A
  N5: U1.K2-In, M1.C
  N6: U1.K2-On, M2.C
  N7: U1.K3-In, M1.B
  N8: U1.K3-On, M2.B
  N9: U1.K4-In, M1.D
  N10: U1.K4-On, M2.D

notes:
  MOTOR DRIVER (DM860A2)
  Green -- (A+)
  Red -- (A-)
  Blue -- (B+)
  Yellow-- (B-)
  MOTOR DRIVER (DM860A2)
  Pin8-- ( DIR + )
  GND-- (DIR -)
  Pin9-- (Pull +)
  GND-- (Pull-)

custom parts:
  4-Channel 5v Relay Shield: 4 Channel 5v Relay Shield w. 2x SPD-06VDC-SD-C
