# Fritzing sketch walker_RCck27CweU (saved by Fritzing 0.9.3b)
breadboards: 1

parts:
  Grove1 = Grove OLED 128x96
  Part1 = Arduino Nano (Rev3.0)
  Part2 = Thumb Joystick
  S1 = SWITCH-MOMENTARY-2 [package=tactile-pth-12mm]
  S2 = SWITCH-MOMENTARY-2 [package=tactile-pth-12mm]
  S3 = SWITCH-MOMENTARY-2 [package=tactile-pth-12mm]
  S4 = SWITCH-MOMENTARY-2 [package=tactile-pth-12mm]
  S5 = SWITCH-MOMENTARY-2 [package=tactile-pth]
  BAT1 = BC9VPC [package=bc9vpc]
  Part3 = Bluetooth HC-05 Macho

nets:
  GND: Grove1.GND, Part1.GND, Part2.GND, S5.2, Part3.GND
  VCC: Grove1.VCC, Part1.5V, Part2.VCC, S1.1, S2.1, S3.1, S4.1, Part3.VCC
  N1: Grove1.SDA, Part1.A4
  N2: Grove1.SCL, Part1.A5
  N3: Part1.D1/TX, Part3.RXD
  N4: Part1.D0/RX, Part3.TXD
  N5: Part1.D2, S1.2
  N6: Part1.D3, S2.2
  N7: Part1.D4, S3.2
  N8: Part1.D5, S4.2
  N9: Part1.VIN, BAT1.V+
  N10: S5.1, BAT1.V-

notes:
  Power button
  Oled screen
